# Fritzing sketch schematic (saved by Fritzing 0.9.2b)
perfboards: 1

parts:
  U1 = ATTINY45 [package=dip]
  R1 = Resistor [tolerance=±5% resistance=4.7k package=THT]
  CAPSENSE1 = AT42QT1010 Momentary Capsense Breakout
  TRS1 = Audio Jack (TRS) 3.5mm [package="PG203J [THT]"]
  R2 = Resistor [tolerance=±5% resistance=4.7k package=THT]

nets:
  N1: U1.PB4(ADC2), TRS1.Ring
  GND: U1.GND, CAPSENSE1.GND, TRS1.Sleeve
  N2: U1.PB0(MOSI), R2.Pin_0
  N3: U1.PB1(MISO), CAPSENSE1.OUT
  N4: U1.PB2(SCK_ADC1), R1.Pin_0
  5V: U1.VCC, R1.Pin_1, CAPSENSE1.VDD, R2.Pin_1

custom parts:
  AT42QT1010 Momentary Capsense Breakout: A capacitive touch momentary switch breakout for the AT42QT1010 chip.
